// Logisim project CS1409_U201414803_许荣仁_mipscpu.circ as structural Verilog
module decoder1 (
  input  o0,
  input  o1,
  input  o2,
  input  o3,
  input  o4,
  input  o5,
  input  f0,
  input  f1,
  input  f2,
  input  f3,
  input  f4,
  input  f5,
  output add,
  output addi,
  output addiu,
  output addu,
  output \and ,
  output andi,
  output sll,
  output sra,
  output srl,
  output sub,
  output \or ,
  output ori
);

  wire not_1_out, not_2_out, not_3_out, not_4_out, not_5_out, not_6_out, not_7_out, not_8_out, not_9_out,
       not_10_out, not_11_out, not_12_out, not_13_out, not_14_out, not_15_out, not_16_out, not_17_out,
       not_18_out, not_19_out, not_20_out, not_21_out, not_22_out, not_23_out, not_24_out, not_25_out,
       not_26_out, not_27_out, not_28_out, not_29_out, not_30_out, not_31_out, not_32_out, not_33_out,
       not_34_out, not_35_out, not_36_out, not_37_out, not_38_out, not_39_out, not_40_out, not_41_out,
       not_42_out, not_43_out, not_44_out, not_45_out, not_46_out, not_47_out, not_48_out, not_49_out,
       not_50_out, not_51_out, not_52_out, not_53_out, not_54_out, not_55_out, not_56_out, not_57_out,
       not_58_out, not_59_out, not_60_out, not_61_out, not_62_out, not_63_out, not_64_out, not_65_out,
       not_66_out, not_67_out, not_68_out, not_69_out, not_70_out, not_71_out, not_72_out, not_73_out,
       not_74_out, not_75_out, not_76_out, not_77_out, not_78_out, not_79_out, not_80_out, not_81_out,
       not_82_out, not_83_out, not_84_out, not_85_out, not_86_out, not_87_out, not_88_out, not_89_out,
       not_90_out, not_91_out, not_92_out, not_93_out, not_94_out, not_95_out, not_96_out, not_97_out,
       not_98_out, not_99_out;

  not not_1 (not_1_out, o0);
  not not_2 (not_2_out, o1);
  not not_3 (not_3_out, o2);
  not not_4 (not_4_out, o3);
  not not_5 (not_5_out, o4);
  not not_6 (not_6_out, o5);
  not not_7 (not_7_out, f1);
  not not_8 (not_8_out, f2);
  not not_9 (not_9_out, f3);
  not not_10 (not_10_out, f4);
  not not_11 (not_11_out, f5);
  not not_12 (not_12_out, o0);
  not not_13 (not_13_out, o1);
  not not_14 (not_14_out, o3);
  not not_15 (not_15_out, o4);
  not not_16 (not_16_out, o5);
  not not_17 (not_17_out, o0);
  not not_18 (not_18_out, o1);
  not not_19 (not_19_out, o3);
  not not_20 (not_20_out, o4);
  not not_21 (not_21_out, o0);
  not not_22 (not_22_out, o1);
  not not_23 (not_23_out, o2);
  not not_24 (not_24_out, o3);
  not not_25 (not_25_out, o4);
  not not_26 (not_26_out, o5);
  not not_27 (not_27_out, f1);
  not not_28 (not_28_out, f2);
  not not_29 (not_29_out, f3);
  not not_30 (not_30_out, f4);
  not not_31 (not_31_out, o0);
  not not_32 (not_32_out, o1);
  not not_33 (not_33_out, o2);
  not not_34 (not_34_out, o3);
  not not_35 (not_35_out, o4);
  not not_36 (not_36_out, o5);
  not not_37 (not_37_out, f1);
  not not_38 (not_38_out, f2);
  not not_39 (not_39_out, f4);
  not not_40 (not_40_out, f5);
  not not_41 (not_41_out, o0);
  not not_42 (not_42_out, o1);
  not not_43 (not_43_out, o4);
  not not_44 (not_44_out, o5);
  not not_45 (not_45_out, o0);
  not not_46 (not_46_out, o1);
  not not_47 (not_47_out, o2);
  not not_48 (not_48_out, o3);
  not not_49 (not_49_out, o4);
  not not_50 (not_50_out, o5);
  not not_51 (not_51_out, f0);
  not not_52 (not_52_out, f1);
  not not_53 (not_53_out, f2);
  not not_54 (not_54_out, f3);
  not not_55 (not_55_out, f4);
  not not_56 (not_56_out, f5);
  not not_57 (not_57_out, o0);
  not not_58 (not_58_out, o1);
  not not_59 (not_59_out, o2);
  not not_60 (not_60_out, o3);
  not not_61 (not_61_out, o4);
  not not_62 (not_62_out, o5);
  not not_63 (not_63_out, f0);
  not not_64 (not_64_out, f1);
  not not_65 (not_65_out, f2);
  not not_66 (not_66_out, f3);
  not not_67 (not_67_out, o0);
  not not_68 (not_68_out, o1);
  not not_69 (not_69_out, o2);
  not not_70 (not_70_out, o3);
  not not_71 (not_71_out, o4);
  not not_72 (not_72_out, o5);
  not not_73 (not_73_out, f0);
  not not_74 (not_74_out, f1);
  not not_75 (not_75_out, f2);
  not not_76 (not_76_out, f3);
  not not_77 (not_77_out, f5);
  not not_78 (not_78_out, o0);
  not not_79 (not_79_out, o1);
  not not_80 (not_80_out, o2);
  not not_81 (not_81_out, o3);
  not not_82 (not_82_out, o4);
  not not_83 (not_83_out, o5);
  not not_84 (not_84_out, f1);
  not not_85 (not_85_out, f2);
  not not_86 (not_86_out, f3);
  not not_87 (not_87_out, f5);
  not not_88 (not_88_out, o0);
  not not_89 (not_89_out, o1);
  not not_90 (not_90_out, o2);
  not not_91 (not_91_out, o3);
  not not_92 (not_92_out, o4);
  not not_93 (not_93_out, o5);
  not not_94 (not_94_out, f1);
  not not_95 (not_95_out, f2);
  not not_96 (not_96_out, f4);
  not not_97 (not_97_out, o0);
  not not_98 (not_98_out, o1);
  not not_99 (not_99_out, o4);
  and and_1 (add, not_1_out, not_2_out, not_3_out, not_4_out, not_5_out, not_6_out, f0, not_7_out, not_8_out, not_9_out, not_10_out, not_11_out);
  and and_2 (addi, not_12_out, not_13_out, o2, not_14_out, not_15_out, not_16_out);
  and and_3 (addiu, not_17_out, not_18_out, o2, not_19_out, not_20_out, o5);
  and and_4 (addu, not_21_out, not_22_out, not_23_out, not_24_out, not_25_out, not_26_out, f0, not_27_out, not_28_out, not_29_out, not_30_out, f5);
  and and_5 (\and , not_31_out, not_32_out, not_33_out, not_34_out, not_35_out, not_36_out, f0, not_37_out, not_38_out, f3, not_39_out, not_40_out);
  and and_6 (andi, not_41_out, not_42_out, o2, o3, not_43_out, not_44_out);
  and and_7 (sll, not_45_out, not_46_out, not_47_out, not_48_out, not_49_out, not_50_out, not_51_out, not_52_out, not_53_out, not_54_out, not_55_out, not_56_out);
  and and_8 (sra, not_57_out, not_58_out, not_59_out, not_60_out, not_61_out, not_62_out, not_63_out, not_64_out, not_65_out, not_66_out, f4, f5);
  and and_9 (srl, not_67_out, not_68_out, not_69_out, not_70_out, not_71_out, not_72_out, not_73_out, not_74_out, not_75_out, not_76_out, f4, not_77_out);
  and and_10 (sub, not_78_out, not_79_out, not_80_out, not_81_out, not_82_out, not_83_out, f0, not_84_out, not_85_out, not_86_out, f4, not_87_out);
  and and_11 (\or , not_88_out, not_89_out, not_90_out, not_91_out, not_92_out, not_93_out, f0, not_94_out, not_95_out, f3, not_96_out, f5);
  and and_12 (ori, not_97_out, not_98_out, o2, o3, not_99_out, o5);
endmodule

module decoder2 (
  input  o0,
  input  o1,
  input  o2,
  input  o3,
  input  o4,
  input  o5,
  input  f0,
  input  f1,
  input  f2,
  input  f3,
  input  f4,
  input  f5,
  output \nor ,
  output lw,
  output sw,
  output beq,
  output bne,
  output slt,
  output slti,
  output sltu,
  output jump,
  output jmpl,
  output jmpr,
  output syscall
);

  wire not_1_out, not_2_out, not_3_out, not_4_out, not_5_out, not_6_out, not_7_out, not_8_out, not_9_out,
       not_10_out, not_11_out, not_12_out, not_13_out, not_14_out, not_15_out, not_16_out, not_17_out,
       not_18_out, not_19_out, not_20_out, not_21_out, not_22_out, not_23_out, not_24_out, not_25_out,
       not_26_out, not_27_out, not_28_out, not_29_out, not_30_out, not_31_out, not_32_out, not_33_out,
       not_34_out, not_35_out, not_36_out, not_37_out, not_38_out, not_39_out, not_40_out, not_41_out,
       not_42_out, not_43_out, not_44_out, not_45_out, not_46_out, not_47_out, not_48_out, not_49_out,
       not_50_out, not_51_out, not_52_out, not_53_out, not_54_out, not_55_out, not_56_out, not_57_out,
       not_58_out, not_59_out, not_60_out, not_61_out, not_62_out, not_63_out, not_64_out, not_65_out,
       not_66_out, not_67_out, not_68_out, not_69_out, not_70_out, not_71_out, not_72_out, not_73_out;

  not not_1 (not_1_out, o0);
  not not_2 (not_2_out, o1);
  not not_3 (not_3_out, o2);
  not not_4 (not_4_out, o3);
  not not_5 (not_5_out, o4);
  not not_6 (not_6_out, o5);
  not not_7 (not_7_out, f1);
  not not_8 (not_8_out, f2);
  not not_9 (not_9_out, o1);
  not not_10 (not_10_out, o2);
  not not_11 (not_11_out, o3);
  not not_12 (not_12_out, o1);
  not not_13 (not_13_out, o3);
  not not_14 (not_14_out, o0);
  not not_15 (not_15_out, o1);
  not not_16 (not_16_out, o2);
  not not_17 (not_17_out, o4);
  not not_18 (not_18_out, o5);
  not not_19 (not_19_out, o0);
  not not_20 (not_20_out, o1);
  not not_21 (not_21_out, o2);
  not not_22 (not_22_out, o4);
  not not_23 (not_23_out, o0);
  not not_24 (not_24_out, o1);
  not not_25 (not_25_out, o2);
  not not_26 (not_26_out, o3);
  not not_27 (not_27_out, o4);
  not not_28 (not_28_out, o5);
  not not_29 (not_29_out, f1);
  not not_30 (not_30_out, f3);
  not not_31 (not_31_out, f5);
  not not_32 (not_32_out, o0);
  not not_33 (not_33_out, o1);
  not not_34 (not_34_out, o3);
  not not_35 (not_35_out, o5);
  not not_36 (not_36_out, o0);
  not not_37 (not_37_out, o1);
  not not_38 (not_38_out, o2);
  not not_39 (not_39_out, o3);
  not not_40 (not_40_out, o4);
  not not_41 (not_41_out, o5);
  not not_42 (not_42_out, f1);
  not not_43 (not_43_out, f3);
  not not_44 (not_44_out, o0);
  not not_45 (not_45_out, o1);
  not not_46 (not_46_out, o2);
  not not_47 (not_47_out, o3);
  not not_48 (not_48_out, o5);
  not not_49 (not_49_out, o0);
  not not_50 (not_50_out, o1);
  not not_51 (not_51_out, o2);
  not not_52 (not_52_out, o3);
  not not_53 (not_53_out, o0);
  not not_54 (not_54_out, o1);
  not not_55 (not_55_out, o2);
  not not_56 (not_56_out, o3);
  not not_57 (not_57_out, o4);
  not not_58 (not_58_out, o5);
  not not_59 (not_59_out, f0);
  not not_60 (not_60_out, f1);
  not not_61 (not_61_out, f3);
  not not_62 (not_62_out, f4);
  not not_63 (not_63_out, f5);
  not not_64 (not_64_out, o0);
  not not_65 (not_65_out, o1);
  not not_66 (not_66_out, o2);
  not not_67 (not_67_out, o3);
  not not_68 (not_68_out, o4);
  not not_69 (not_69_out, o5);
  not not_70 (not_70_out, f0);
  not not_71 (not_71_out, f1);
  not not_72 (not_72_out, f4);
  not not_73 (not_73_out, f5);
  and and_1 (\nor , not_1_out, not_2_out, not_3_out, not_4_out, not_5_out, not_6_out, f0, not_7_out, not_8_out, f3, f4, f5);
  and and_2 (lw, o0, not_9_out, not_10_out, not_11_out, o4, o5);
  and and_3 (sw, o0, not_12_out, o2, not_13_out, o4, o5);
  and and_4 (beq, not_14_out, not_15_out, not_16_out, o3, not_17_out, not_18_out);
  and and_5 (bne, not_19_out, not_20_out, not_21_out, o3, not_22_out, o5);
  and and_6 (slt, not_23_out, not_24_out, not_25_out, not_26_out, not_27_out, not_28_out, f0, not_29_out, f2, not_30_out, f4, not_31_out);
  and and_7 (slti, not_32_out, not_33_out, o2, not_34_out, o4, not_35_out);
  and and_8 (sltu, not_36_out, not_37_out, not_38_out, not_39_out, not_40_out, not_41_out, f0, not_42_out, f2, not_43_out, f4, f5);
  and and_9 (jump, not_44_out, not_45_out, not_46_out, not_47_out, o4, not_48_out);
  and and_10 (jmpl, not_49_out, not_50_out, not_51_out, not_52_out, o4, o5);
  and and_11 (jmpr, not_53_out, not_54_out, not_55_out, not_56_out, not_57_out, not_58_out, not_59_out, not_60_out, f2, not_61_out, not_62_out, not_63_out);
  and and_12 (syscall, not_64_out, not_65_out, not_66_out, not_67_out, not_68_out, not_69_out, not_70_out, not_71_out, f2, f3, not_72_out, not_73_out);
endmodule
